# Fritzing sketch practice06 (saved by Fritzing 0.9.5d)
breadboards: 1

parts:
  U1 = LuaNode32 / ESP32 [part_number=ESP32S-PIN30]
  PIR1 = PIR sensor

nets:
  GND: U1.GND, PIR1.GND
  3V3: U1.3V3, PIR1.VDD
  N1: U1.D4, PIR1.SIG

custom parts:
  LuaNode32 / ESP32: New Image for LuaNode32 DOIT ESP32 DEVKIT V1. Base parts from LuaNode32 / ESP32 ESP32 based LuaNode32 by G.Noorlander DOIT Esp32 DevKit v1 (30 pins long, 11 pins width) by Werner Rothschopf (modified by vanepp Dec 2018)
